// Digital circuit ALU.dig as structural Verilog
module ALU (
  input  [15:0] A,
  input  [15:0] B,
  input  [2:0] ALU_FUNC,
  output [15:0] RESULT,
  output Z,
  output N,
  output C,
  output V
);

  wire ADD_CARRY, and_2_out, and_3_out, not_2_out, SUB_mode, xnor_1_out, xor_2_out, xor_3_out, xor_4_out;
  wire [15:0] addR, and_1_out, multiplexer_1_out, not_1_out, or_1_out, SHL_out, SHR_out, xor_1_out;

  assign not_1_out = ~B;  // Not not_1, 16 bits wide
  Multiplexer #(.Bits(16)) multiplexer_1 (.sel(SUB_mode), .in_0(B), .in_1(not_1_out), .out(multiplexer_1_out));
  Comparator #(.Bits(3)) comparator_1 (.a(ALU_FUNC), .b(3'b001), .eq(SUB_mode));  // open: gt, lt
  Add #(.Bits(16)) ADD (.a(A), .b(multiplexer_1_out), .c_i(SUB_mode), .s(addR), .c_o(ADD_CARRY));
  assign and_1_out = A & B;  // And and_1, 16 bits wide
  assign or_1_out = A | B;  // Or or_1, 16 bits wide
  assign xor_1_out = A ^ B;  // XOr xor_1, 16 bits wide
  BarrelShifter #(.Bits(16)) SHL (.in(A), .shift({1'b0, B[3:0]}), .out(SHL_out));
  BarrelShifter #(.Bits(16), .direction("right")) SHR (.in(A), .shift({1'b0, B[3:0]}), .out(SHR_out));
  Multiplexer #(.Selector_Bits(3), .Bits(16)) multiplexer_2 (
    .sel(ALU_FUNC), .in_0(addR), .in_1(addR), .in_2(and_1_out), .in_3(or_1_out), .in_4(xor_1_out),
    .in_5(SHL_out), .in_6(SHR_out), .in_7({16{1'b0}}), .out({N, RESULT[14:0]}));
  Comparator #(.Bits(16)) comparator_2 (.a({N, RESULT[14:0]}), .b({16{1'b0}}), .eq(Z));  // open: gt, lt
  not not_2 (not_2_out, ADD_CARRY);
  Multiplexer #(.Selector_Bits(3)) multiplexer_3 (
    .sel(ALU_FUNC), .in_0(ADD_CARRY), .in_1(not_2_out), .in_2(1'b0), .in_3(1'b0), .in_4(1'b0), .in_5(1'b0),
    .in_6(1'b0), .in_7(1'b0), .out(C));
  xnor xnor_1 (xnor_1_out, A[15], B[15]);
  xor xor_2 (xor_2_out, A[15], addR[15]);
  xor xor_3 (xor_3_out, A[15], B[15]);
  xor xor_4 (xor_4_out, A[15], addR[15]);
  and and_2 (and_2_out, xnor_1_out, xor_2_out);
  and and_3 (and_3_out, xor_3_out, xor_4_out);
  Multiplexer #(.Selector_Bits(3)) multiplexer_4 (
    .sel(ALU_FUNC), .in_0(and_2_out), .in_1(and_3_out), .in_2(1'b0), .in_3(1'b0), .in_4(1'b0), .in_5(1'b0),
    .in_6(1'b0), .in_7(1'b0), .out(V));

  assign RESULT[15] = N;

  // Other names for the same wires on the sheet: sign_A = A[15]; sign_B = B[15]; SUB_CARRY = ADD_CARRY;
  //   subR[15:0] = addR; sign_ADD = addR[15]; sign_SUB = addR[15]
endmodule
