// Digital circuit ConditionEvaluator.dig as structural Verilog
module ConditionEvaluator (
  input  [1:0] CC,
  input  Z,
  input  N,
  input  V,
  output COND_MET
);

  Multiplexer #(.Selector_Bits(2)) multiplexer_1 (.sel(CC), .in_0(1'b1), .in_1(Z), .in_2(N), .in_3(V), .out(COND_MET));
endmodule
