// Digital circuit ControlUnit.dig as structural Verilog
module ControlUnit (
  input  [3:0] OPCODE,
  output FLAG_CAPABLE,
  output REG_WRITE,
  output MEM_WRITE,
  output REG_DST,
  output ALU_A_SEL,
  output [1:0] WB_SEL,
  output [1:0] PC_SEL,
  output [1:0] ALU_B_SEL,
  output [2:0] ALU_FUNC
);

  wire [1:0] rom_1_d;

  ROM #(.AddrBits(4), .Bits(16)) rom_1 (
    .A(OPCODE), .sel(1'b1),
    .D({REG_WRITE, MEM_WRITE, FLAG_CAPABLE, REG_DST, WB_SEL, PC_SEL, ALU_A_SEL, ALU_B_SEL, ALU_FUNC, rom_1_d}));

  // Notes on the sheet:
  //   contents of rom_1 (hex, n*v repeats v):
  //   a000,a004,a008,a00c,a010,a014,a018,8020,8420,4020,80c0,8800,100
  //   ,9d00,200
endmodule
