// Digital circuit DataMemory.dig as structural Verilog
module DataMemory (
  input  CLK,
  input  [15:0] ADDR,
  input  [15:0] WDATA,
  input  MEM_WRITE,
  input  [15:0] MADDR_DBG,
  output [15:0] RDATA,
  output [15:0] DBG_MOUT
);

  RAMDualAccess #(.AddrBits(16), .Bits(16)) DMEM (
    .str(MEM_WRITE), .C(CLK), .ld(1'b1), .A1(ADDR), .Din1(WDATA), .A2(MADDR_DBG), .D1(RDATA), .D2(DBG_MOUT));
endmodule
