// Digital circuit FlagRegister.dig as structural Verilog
module FlagRegister (
  input  CLK,
  input  RESET,
  input  FLAG_WRITE,
  input  Z_IN,
  input  C_IN,
  input  V_IN,
  input  N_IN,
  output [3:0] FLAGS_OUT,
  output Z_OUT,
  output N_OUT,
  output C_OUT,
  output V_OUT
);

  wire or_1_out;
  wire [3:0] multiplexer_1_out;

  Multiplexer #(.Bits(4)) multiplexer_1 (
    .sel(RESET), .in_0({V_IN, C_IN, N_IN, Z_IN}), .in_1(4'b0000), .out(multiplexer_1_out));
  or or_1 (or_1_out, FLAG_WRITE, RESET);
  Register #(.Bits(4)) register_1 (
    .D(multiplexer_1_out), .C(CLK), .en(or_1_out), .Q({FLAGS_OUT[3], C_OUT, FLAGS_OUT[1:0]}));

  assign FLAGS_OUT[2] = C_OUT;
  assign N_OUT = FLAGS_OUT[1];
  assign V_OUT = FLAGS_OUT[3];
  assign Z_OUT = FLAGS_OUT[0];

  // Other names for the same wires on the sheet: NEW_FLAGS[3:0] = {V_IN, C_IN, N_IN, Z_IN}; FW = FLAG_WRITE
endmodule
