// Digital circuit Pars16.dig as structural Verilog
module Pars16 (
  input  CLK,
  input  [2:0] DBG_RSEL,
  input  RESET,
  input  DBG_EN,
  input  [15:0] DBG_MADDR,
  output [7:0] PC_OUT,
  output [15:0] IR_OUT,
  output [3:0] FLAGS_OUT,
  output [15:0] DBG_MOUT,
  output [15:0] DBG_ROUT
);

  wire ALU_A_SEL, ALU_C, ALU_N, ALU_V, ALU_Z, and_3_out, COND_MET, FLAG_CAPABLE, flagregister_1_n_out,
       flagregister_1_v_out, flagregister_1_z_out, MEM_WRITE_FINAL, MEM_WRITE_RAW, REG_DST, REG_WRITE_FINAL,
       REG_WRITE_RAW;
  wire [1:0] ALU_B_SEL, PC_SEL, PC_SEL_FINAL, WB_SEL;
  wire [2:0] ALU_FUNC, multiplexer_1_out, multiplexer_2_out, multiplexer_3_out, multiplexer_6_out;
  wire [7:0] JR_TARGET, multiplexer_5_out, PC_NEXT, PC_p_16, REL_TARGET;
  wire [15:0] ALU_RESULT, IMM4_EXT, IMM7_EXT, multiplexer_4_out, multiplexer_9_out, multiplexer_10_out,
       OFFSET10_EXT, RDATA, RS2_DATA;
  wire [15:8] REL_TARGET_16, RS1_DATA;

  Multiplexer #(.Bits(3)) multiplexer_1 (.sel(REG_DST), .in_0(IR_OUT[9:7]), .in_1(3'b111), .out(multiplexer_1_out));
  Multiplexer #(.Bits(3)) multiplexer_2 (
    .sel(PC_SEL[1]), .in_0(IR_OUT[6:4]), .in_1(IR_OUT[9:7]), .out(multiplexer_2_out));
  Multiplexer #(.Bits(3)) multiplexer_3 (
    .sel(MEM_WRITE_RAW), .in_0(IR_OUT[3:1]), .in_1(IR_OUT[9:7]), .out(multiplexer_3_out));
  Multiplexer #(.Selector_Bits(2), .Bits(16)) multiplexer_4 (
    .sel(WB_SEL), .in_0(ALU_RESULT), .in_1(RDATA), .in_2({IR_OUT[6:0], {9{1'b0}}}),
    .in_3({{8{1'b0}}, PC_p_16}), .out(multiplexer_4_out));
  Multiplexer #(.Bits(8)) multiplexer_5 (.sel(RESET), .in_0(PC_NEXT), .in_1({8{1'b0}}), .out(multiplexer_5_out));
  Multiplexer #(.Bits(3)) multiplexer_6 (
    .sel(DBG_EN), .in_0(multiplexer_3_out), .in_1(DBG_RSEL), .out(multiplexer_6_out));
  Register #(.Bits(8)) PC (.D(multiplexer_5_out), .C(CLK), .en(1'b1), .Q(PC_OUT));
  RegisterFile registerfile_1 ();
  // Probe on PC_OUT
  Add #(.Bits(8)) add_1 (.a(PC_OUT), .b(8'h1), .c_i(1'b0), .s(PC_p_16));  // open: c_o
  ROM #(.AddrBits(8), .isProgramMemory("true"), .Bits(16)) Instruction_ROM (.A(PC_OUT), .sel(1'b1), .D(IR_OUT));
  SignExtend signextend_1 ();
  DataMemory datamemory_1 (
    .CLK(CLK), .ADDR(ALU_RESULT), .WDATA(RS2_DATA), .MEM_WRITE(MEM_WRITE_FINAL), .MADDR_DBG(DBG_MADDR),
    .RDATA(RDATA), .DBG_MOUT(DBG_MOUT));
  // Probe offset10 on IR_OUT[9:0]
  // Probe cc on IR_OUT[15:14]
  // Probe opcode on IR_OUT[13:10]
  ControlUnit controlunit_1 (
    .OPCODE(IR_OUT[13:10]), .FLAG_CAPABLE(FLAG_CAPABLE), .REG_WRITE(REG_WRITE_RAW),
    .MEM_WRITE(MEM_WRITE_RAW), .REG_DST(REG_DST), .ALU_A_SEL(ALU_A_SEL), .WB_SEL(WB_SEL), .PC_SEL(PC_SEL),
    .ALU_B_SEL(ALU_B_SEL), .ALU_FUNC(ALU_FUNC));
  Multiplexer #(.Bits(2)) multiplexer_7 (.sel(COND_MET), .in_0(2'b00), .in_1(PC_SEL), .out(PC_SEL_FINAL));
  Add #(.Bits(16)) add_2 (
    .a({{8{1'b0}}, PC_p_16}), .b(OFFSET10_EXT), .c_i(1'b0), .s({REL_TARGET_16, REL_TARGET}));  // open: c_o
  and and_1 (REG_WRITE_FINAL, REG_WRITE_RAW, COND_MET);
  and and_2 (MEM_WRITE_FINAL, MEM_WRITE_RAW, COND_MET);
  // Probe REG_WRITE_FINAL on REG_WRITE_FINAL
  // Probe MEM_WRITE_FINAL on MEM_WRITE_FINAL
  Multiplexer #(.Selector_Bits(2), .Bits(8)) multiplexer_8 (
    .sel(PC_SEL_FINAL), .in_0(PC_p_16), .in_1(REL_TARGET), .in_2(JR_TARGET), .in_3(PC_p_16), .out(PC_NEXT));
  and and_3 (and_3_out, COND_MET, IR_OUT[0], FLAG_CAPABLE);
  Multiplexer #(.Bits(16)) multiplexer_9 (
    .sel(ALU_A_SEL), .in_0({RS1_DATA, JR_TARGET}), .in_1({16{1'b0}}), .out(multiplexer_9_out));
  Multiplexer #(.Selector_Bits(2), .Bits(16)) multiplexer_10 (
    .sel(ALU_B_SEL), .in_0(RS2_DATA), .in_1(IMM4_EXT), .in_2(IMM7_EXT), .in_3({16{1'b0}}),
    .out(multiplexer_10_out));
  FlagRegister flagregister_1 (
    .CLK(CLK), .RESET(RESET), .FLAG_WRITE(and_3_out), .Z_IN(ALU_Z), .C_IN(ALU_C), .V_IN(ALU_V), .N_IN(ALU_N),
    .FLAGS_OUT(FLAGS_OUT), .Z_OUT(flagregister_1_z_out), .N_OUT(flagregister_1_n_out),
    .V_OUT(flagregister_1_v_out));  // open: C_OUT
  ALU alu_1 ();
  // Probe ALU_result on ALU_RESULT
  ConditionEvaluator conditionevaluator_1 (
    .CC(IR_OUT[15:14]), .Z(flagregister_1_z_out), .N(flagregister_1_n_out), .V(flagregister_1_v_out),
    .COND_MET(COND_MET));
  // Probe COND_MET on COND_MET

  // Other names for the same wires on the sheet: IMM4[3:0] = IR_OUT[3:0]; IMM7[6:0] = IR_OUT[6:0];
  //   LUI_RESULT[15:9] = IR_OUT[6:0]; OFFSET10[9:0] = IR_OUT[9:0]; S = IR_OUT[0]; FIELD_3_1[2:0] = IR_OUT[3:1];
  //   FIELD_6_4[2:0] = IR_OUT[6:4]; FIELD_9_7[2:0] = IR_OUT[9:7]; OPCODE[3:0] = IR_OUT[13:10];
  //   CC[1:0] = IR_OUT[15:14]; MADDR_DBG[15:0] = DBG_MADDR; PC_PLUS_1[7:0] = PC_p_16; REL_TARGET_16[7:0] = REL_TARGET;
  //   RS1_DATA[7:0] = JR_TARGET

  // Notes on the sheet:
  //   contents of Instruction_ROM (hex, n*v repeats v):
  //   2885,2907,0195,2580,2200,06c7,6b01,ab02,7001,2b03,3402,3003,3c00,1f61,3b80,33ff
endmodule
