// Digital circuit RegisterFile.dig as structural Verilog
module RegisterFile (
  input  [2:0] DBG_RSEL,
  input  [2:0] WADDR,
  input  [2:0] RADDR1,
  input  [2:0] RADDR2,
  input  [15:0] WDATA,
  input  CLK,
  input  WE,
  input  RESET,
  output [15:0] DBG_ROUT,
  output [15:0] RDATA1,
  output [15:0] RDATA2
);

  wire D1, D2, D3, D4, D5, D6, D7, Enable_1, Enable_2, Enable_3, Enable_4, Enable_5, Enable_6, Enable_7,
       Write_1, Write_2, Write_3, Write_4, Write_5, Write_6, Write_7;
  wire [15:0] D, R1_Q, R2_Q, R3_Q, R4_Q, R5_Q, R6_Q, R7_Q;

  Multiplexer #(.Bits(16)) multiplexer_1 (.sel(RESET), .in_0(WDATA), .in_1({16{1'b0}}), .out(D));
  Decoder #(.Selector_Bits(3)) decoder_1 (
    .sel(WADDR), .out_1(D1), .out_2(D2), .out_3(D3), .out_4(D4), .out_5(D5), .out_6(D6), .out_7(D7));  // open: out_0
  Register #(.Bits(16)) R1 (.D(D), .C(CLK), .en(Enable_1), .Q(R1_Q));
  Register #(.Bits(16)) R2 (.D(D), .C(CLK), .en(Enable_2), .Q(R2_Q));
  Register #(.Bits(16)) R3 (.D(D), .C(CLK), .en(Enable_3), .Q(R3_Q));
  Register #(.Bits(16)) R4 (.D(D), .C(CLK), .en(Enable_4), .Q(R4_Q));
  Register #(.Bits(16)) R5 (.D(D), .C(CLK), .en(Enable_5), .Q(R5_Q));
  Register #(.Bits(16)) R6 (.D(D), .C(CLK), .en(Enable_6), .Q(R6_Q));
  Register #(.Bits(16)) R7 (.D(D), .C(CLK), .en(Enable_7), .Q(R7_Q));
  and and_1 (Write_1, D1, WE);
  and and_2 (Write_2, D2, WE);
  and and_3 (Write_3, D3, WE);
  Multiplexer #(.Selector_Bits(3), .Bits(16)) multiplexer_2 (
    .sel(RADDR1), .in_0({16{1'b0}}), .in_1(R1_Q), .in_2(R2_Q), .in_3(R3_Q), .in_4(R4_Q), .in_5(R5_Q),
    .in_6(R6_Q), .in_7(R7_Q), .out(RDATA1));
  and and_4 (Write_4, D4, WE);
  and and_5 (Write_5, D5, WE);
  and and_6 (Write_6, D6, WE);
  and and_7 (Write_7, D7, WE);
  Multiplexer #(.Selector_Bits(3), .Bits(16)) multiplexer_3 (
    .sel(RADDR2), .in_0({16{1'b0}}), .in_1(R1_Q), .in_2(R2_Q), .in_3(R3_Q), .in_4(R4_Q), .in_5(R5_Q),
    .in_6(R6_Q), .in_7(R7_Q), .out(RDATA2));
  or or_1 (Enable_1, Write_1, RESET);
  or or_2 (Enable_2, Write_2, RESET);
  or or_3 (Enable_3, Write_3, RESET);
  Multiplexer #(.Bits(16), .Selector_Bits(3)) multiplexer_4 (
    .sel(DBG_RSEL), .in_0({16{1'b0}}), .in_1(R1_Q), .in_2(R2_Q), .in_3(R3_Q), .in_4(R4_Q), .in_5(R5_Q),
    .in_6(R6_Q), .in_7(R7_Q), .out(DBG_ROUT));
  or or_4 (Enable_4, Write_4, RESET);
  or or_5 (Enable_5, Write_5, RESET);
  or or_6 (Enable_6, Write_6, RESET);
  or or_7 (Enable_7, Write_7, RESET);
endmodule
