// Digital circuit SignExtend.dig as structural Verilog
module SignExtend (
  input  [3:0] IMM4_IN,
  input  [6:0] IMM7_IN,
  input  [9:0] OFFSET10_IN,
  output [15:0] IMM4_EXT,
  output [15:0] IMM7_EXT,
  output [15:0] OFFSET10_EXT
);

  BitExtender #(.inputBits(4)) bitextender_1 (.in(IMM4_IN), .out(IMM4_EXT));
  BitExtender #(.inputBits(7)) bitextender_2 (.in(IMM7_IN), .out(IMM7_EXT));
  BitExtender #(.inputBits(10)) bitextender_3 (.in(OFFSET10_IN), .out(OFFSET10_EXT));
endmodule
